// Digital circuit 1bitLogicALU.dig as structural Verilog
module _1bitLogicALU (
  input  A,
  input  B,
  output A_and_B,
  output A_or_B,
  output A_xor_B
);

  and and_1 (A_and_B, A, B);
  or or_1 (A_or_B, A, B);
  xor xor_1 (A_xor_B, A, B);
endmodule
