// Digital circuit 2x4bitMux.dig as structural Verilog
module _2x4bitMux (
  input  [3:0] A,
  input  [3:0] B,
  input  E,
  output [3:0] out
);

  wire [3:0] and_1_out, and_2_out, not_1_out;

  assign not_1_out = ~{4{E}};  // Not not_1, 4 bits wide
  assign and_1_out = {4{E}} & A;  // And and_1, 4 bits wide
  assign and_2_out = B & not_1_out;  // And and_2, 4 bits wide
  assign out = and_1_out | and_2_out;  // Or or_1, 4 bits wide
endmodule
