// Digital circuit 4bit-register.dig as structural Verilog
module _4bit_register (
  input  CK,
  input  Write_enable,
  input  [3:0] D_bus_4bit,
  input  R,
  output [3:0] Q_bus_4bit
);

  FlipFlop_D flipflop_d_1 (
    .CK(CK), .D(D_bus_4bit[0]), .Write_enable(Write_enable), .R(R), .Q(Q_bus_4bit[0]));  // open: Q_2
  FlipFlop_D flipflop_d_2 (
    .CK(CK), .D(D_bus_4bit[1]), .Write_enable(Write_enable), .R(R), .Q(Q_bus_4bit[1]));  // open: Q_2
  FlipFlop_D flipflop_d_3 (
    .CK(CK), .D(D_bus_4bit[2]), .Write_enable(Write_enable), .R(R), .Q(Q_bus_4bit[2]));  // open: Q_2
  FlipFlop_D flipflop_d_4 (
    .CK(CK), .D(D_bus_4bit[3]), .Write_enable(Write_enable), .R(R), .Q(Q_bus_4bit[3]));  // open: Q_2
  // Pins of 1 and 4 bits meet at D_bus_4bit
  // Pins of 1 and 4 bits meet at Q_bus_4bit

  // Other names for the same wires on the sheet: d1 = D_bus_4bit[0]; d2 = D_bus_4bit[1]; d3 = D_bus_4bit[2];
  //   d4 = D_bus_4bit[3]
endmodule
