// Digital circuit 4bitAdder.dig as structural Verilog
module _4bitAdder (
  input  A1,
  input  B1,
  input  carry_in,
  input  A2,
  input  B2,
  input  A3,
  input  B3,
  input  A4,
  input  B4,
  output X1,
  output X2,
  output X3,
  output X4,
  output carry_out
);

  wire and_1_out, and_2_out, and_3_out, and_4_out, and_5_out, and_6_out, and_7_out, and_8_out, or_1_out,
       or_2_out, or_3_out, xor_1_out, xor_2_out, xor_3_out, xor_4_out;

  xor xor_1 (xor_1_out, A1, B1);
  xor xor_2 (xor_2_out, A2, B2);
  xor xor_3 (xor_3_out, A3, B3);
  xor xor_4 (xor_4_out, A4, B4);
  xor xor_5 (X1, xor_1_out, carry_in);
  and and_1 (and_1_out, carry_in, xor_1_out);
  and and_2 (and_2_out, A1, B1);
  xor xor_6 (X2, xor_2_out, or_1_out);
  and and_3 (and_3_out, or_1_out, xor_2_out);
  and and_4 (and_4_out, A2, B2);
  xor xor_7 (X3, xor_3_out, or_2_out);
  and and_5 (and_5_out, or_2_out, xor_3_out);
  and and_6 (and_6_out, A3, B3);
  xor xor_8 (X4, xor_4_out, or_3_out);
  and and_7 (and_7_out, or_3_out, xor_4_out);
  and and_8 (and_8_out, A4, B4);
  or or_1 (or_1_out, and_1_out, and_2_out);
  or or_2 (or_2_out, and_3_out, and_4_out);
  or or_3 (or_3_out, and_5_out, and_6_out);
  or or_4 (carry_out, and_7_out, and_8_out);
endmodule
