// Digital circuit 4x4bitDeMux.dig as structural Verilog
module _4x4bitDeMux (
  input  S0,
  input  S1,
  input  [3:0] _4b_in,
  output [3:0] _4b_o1,
  output [3:0] _4b_o2,
  output [3:0] _4b_o3,
  output [3:0] _4b_o4
);

  wire not_1_out, not_2_out;
  wire [3:3] and_1_out, and_2_out, and_3_out, and_4_out;

  not not_1 (not_1_out, S0);
  not not_2 (not_2_out, S1);
  and and_1 (and_1_out[3], S0, S1);
  and and_2 (and_2_out[3], not_1_out, S1);
  and and_3 (and_3_out[3], S0, not_2_out);
  and and_4 (and_4_out[3], not_1_out, not_2_out);
  assign _4b_o1 = {4{and_1_out[3]}} & _4b_in;  // And and_5, 4 bits wide
  assign _4b_o2 = {4{and_2_out[3]}} & _4b_in;  // And and_6, 4 bits wide
  assign _4b_o3 = {4{and_3_out[3]}} & _4b_in;  // And and_7, 4 bits wide
  assign _4b_o4 = {4{and_4_out[3]}} & _4b_in;  // And and_8, 4 bits wide
endmodule
