// Digital circuit 4x4bitMux.dig as structural Verilog
module _4x4bitMux (
  input  S0,
  input  S1,
  input  [3:0] _4b_i1,
  input  [3:0] _4b_i2,
  input  [3:0] _4b_i3,
  input  [3:0] _4b_i4,
  output [3:0] _4b_out
);

  wire not_1_out, not_2_out;
  wire [3:0] and_5_out, and_6_out, and_7_out, and_8_out;
  wire [3:3] and_1_out, and_2_out, and_3_out, and_4_out;

  not not_1 (not_1_out, S0);
  not not_2 (not_2_out, S1);
  and and_1 (and_1_out[3], S0, S1);
  and and_2 (and_2_out[3], not_1_out, S1);
  and and_3 (and_3_out[3], S0, not_2_out);
  and and_4 (and_4_out[3], not_1_out, not_2_out);
  assign and_5_out = {4{and_1_out[3]}} & _4b_i1;  // And and_5, 4 bits wide
  assign and_6_out = {4{and_2_out[3]}} & _4b_i2;  // And and_6, 4 bits wide
  assign and_7_out = {4{and_3_out[3]}} & _4b_i3;  // And and_7, 4 bits wide
  assign and_8_out = {4{and_4_out[3]}} & _4b_i4;  // And and_8, 4 bits wide
  assign _4b_out = and_5_out | and_6_out | and_7_out | and_8_out;  // Or or_1, 4 bits wide
endmodule
