// Digital circuit 4x4bit_Registers.dig as structural Verilog
module _4x4bit_Registers (
  input  CK,
  input  S0,
  input  S1,
  input  Write_enable,
  input  [3:0] _4b_in,
  input  S2,
  input  S3,
  input  S4,
  input  S5,
  input  R,
  output [3:0] _4b_out_2,
  output [3:0] _4b_out_1
);

  wire _4x4bitdemux_1_p4, _4x4bitdemux_1_p5, _4x4bitdemux_1_p6, _4x4bitdemux_1_p7;
  wire [3:0] out_1, out_2, out_3, out_4;

  // _4x4bitDeMux _4x4bitdemux_1: pin names not known; wires that end beside it: S0, S1, _4b_in, _4x4bitdemux_1_p4, _4x4bitdemux_1_p5, _4x4bitdemux_1_p6, _4x4bitdemux_1_p7
  // _4bit_register _4bit_register_1: pin names not known; wires that end beside it: CK, Write_enable, _4x4bitdemux_1_p4, R, out_1
  // _4bit_register _4bit_register_2: pin names not known; wires that end beside it: CK, Write_enable, _4x4bitdemux_1_p5, R, out_2
  // _4bit_register _4bit_register_3: pin names not known; wires that end beside it: CK, Write_enable, _4x4bitdemux_1_p6, R, out_3
  // _4bit_register _4bit_register_4: pin names not known; wires that end beside it: CK, Write_enable, _4x4bitdemux_1_p7, R, out_4
  _4x4bitMux _4x4bitmux_1 (
    .S0(S2), .S1(S3), ._4b_i1(out_1), ._4b_i2(out_2), ._4b_i3(out_3), ._4b_i4(out_4), ._4b_out(_4b_out_1));
  _4x4bitMux _4x4bitmux_2 (
    .S0(S4), .S1(S5), ._4b_i1(out_1), ._4b_i2(out_2), ._4b_i3(out_3), ._4b_i4(out_4), ._4b_out(_4b_out_2));

  // Other names for the same wires on the sheet: we = Write_enable
endmodule
