// Digital circuit 8bit_register.dig as structural Verilog
module _8bit_register (
  input  CK,
  input  Write_enable,
  input  [7:0] D_bus,
  output [7:0] Q_bus
);

  FlipFlop_D flipflop_d_1 (.CK(CK), .D(D_bus[0]), .Write_enable(Write_enable), .Q(Q_bus[0]));  // open: R, Q_2
  FlipFlop_D flipflop_d_2 (.CK(CK), .D(D_bus[1]), .Write_enable(Write_enable), .Q(Q_bus[1]));  // open: R, Q_2
  FlipFlop_D flipflop_d_3 (.CK(CK), .D(D_bus[2]), .Write_enable(Write_enable), .Q(Q_bus[2]));  // open: R, Q_2
  FlipFlop_D flipflop_d_4 (.CK(CK), .D(D_bus[3]), .Write_enable(Write_enable), .Q(Q_bus[3]));  // open: R, Q_2
  FlipFlop_D flipflop_d_5 (.CK(CK), .D(D_bus[4]), .Write_enable(Write_enable), .Q(Q_bus[4]));  // open: R, Q_2
  FlipFlop_D flipflop_d_6 (.CK(CK), .D(D_bus[5]), .Write_enable(Write_enable), .Q(Q_bus[5]));  // open: R, Q_2
  FlipFlop_D flipflop_d_7 (.CK(CK), .D(D_bus[6]), .Write_enable(Write_enable), .Q(Q_bus[6]));  // open: R, Q_2
  FlipFlop_D flipflop_d_8 (.CK(CK), .D(D_bus[7]), .Write_enable(Write_enable), .Q(Q_bus[7]));  // open: R, Q_2
  // Pins of 1 and 8 bits meet at D_bus
  // Pins of 1 and 8 bits meet at Q_bus

  // Other names for the same wires on the sheet: d1 = D_bus[0]; d2 = D_bus[1]; d3 = D_bus[2]; d4 = D_bus[3];
  //   d5 = D_bus[4]; d6 = D_bus[5]; d7 = D_bus[6]; d8 = D_bus[7]
endmodule
