// Digital circuit ALU.dig as structural Verilog
module ALU (
  input  carry_in,
  input  S0_alu,
  input  S1_alu,
  input  [3:0] A,
  input  [3:0] B,
  output carry_out,
  output [3:0] out
);

  wire and1, and2, and3, and4, or1, or2, or3, or4, sum1, sum2, sum3, sum4, xor1, xor2, xor3, xor4;

  _1bitLogicALU _1bitlogicalu_1 (.A(A[0]), .B(B[0]), .A_and_B(and1), .A_or_B(or1), .A_xor_B(xor1));
  _1bitLogicALU _1bitlogicalu_2 (.A(A[1]), .B(B[1]), .A_and_B(and2), .A_or_B(or2), .A_xor_B(xor2));
  _1bitLogicALU _1bitlogicalu_3 (.A(A[2]), .B(B[2]), .A_and_B(and3), .A_or_B(or3), .A_xor_B(xor3));
  _1bitLogicALU _1bitlogicalu_4 (.A(A[3]), .B(B[3]), .A_and_B(and4), .A_or_B(or4), .A_xor_B(xor4));
  _4bitAdder _4bitadder_1 (
    .A1(A[0]), .B1(B[0]), .carry_in(carry_in), .A2(A[1]), .B2(B[1]), .A3(A[2]), .B3(B[2]), .A4(A[3]),
    .B4(B[3]), .X1(sum1), .X2(sum2), .X3(sum3), .X4(sum4), .carry_out(carry_out));
  _4bitmux _4bitmux_1 (.S0(S0_alu), .S1(S1_alu), .I1(sum1), .I2(and1), .I3(or1), .I4(xor1), .out(out[0]));
  _4bitmux _4bitmux_2 (.S0(S0_alu), .S1(S1_alu), .I1(sum2), .I2(and2), .I3(or2), .I4(xor2), .out(out[1]));
  _4bitmux _4bitmux_3 (.S0(S0_alu), .S1(S1_alu), .I1(sum3), .I2(and3), .I3(or3), .I4(xor3), .out(out[2]));
  _4bitmux _4bitmux_4 (.S0(S0_alu), .S1(S1_alu), .I1(sum4), .I2(and4), .I3(or4), .I4(xor4), .out(out[3]));

  // Other names for the same wires on the sheet: a1 = A[0]; a2 = A[1]; a3 = A[2]; a4 = A[3]; b1 = B[0]; b2 = B[1];
  //   b3 = B[2]; b4 = B[3]
endmodule
