// Digital circuit CPU.dig as structural Verilog
module CPU (
  input  CK
);

  wire logic_1_p10, logic_1_p12, not_1_out, pc_WE, programcounter_1_p4, ram_OE, register_WE, s0, s1, s2, s3,
       s4, s5, s6, s7;
  wire [3:0] _2x4bitmux_1_out, _4x4bit_registers_1__4b_out_2, alu_1_out, logic_1_p2, ramdualport_1_d;
  wire [7:0] logic_1_p1, programcounter_1_p3, programcounter_1_p5;

  // logic logic_1: pin names not known; wires that end beside it: logic_1_p1, logic_1_p2, s0, s1, s2, s3, s4, s5, register_WE, logic_1_p10, ram_OE, logic_1_p12, pc_WE, s6, s7
  ALU alu_1 (
    .carry_in(logic_1_p12), .S0_alu(s6), .S1_alu(s7), .A(logic_1_p2), .B(_4x4bit_registers_1__4b_out_2),
    .out(alu_1_out));  // open: carry_out
  _2x4bitMux _2x4bitmux_1 (.A(alu_1_out), .B(ramdualport_1_d), .E(not_1_out), .out(_2x4bitmux_1_out));
  not not_1 (not_1_out, ram_OE);
  EEPROM #(.AddrBits(8), .isProgramMemory("true"), .Bits(8)) eeprom_1 (
    .A(programcounter_1_p5), .CS(1'b1), .WE(1'b0), .OE(1'b1), .D(logic_1_p1));
  _4x4bit_Registers _4x4bit_registers_1 (
    .CK(CK), .S0(s0), .S1(s1), .Write_enable(register_WE), ._4b_in(_2x4bitmux_1_out), .S2(s2), .S3(s3),
    .S4(s4), .S5(s5), .R(programcounter_1_p4), ._4b_out_2(_4x4bit_registers_1__4b_out_2),
    ._4b_out_1(logic_1_p2));
  LED led_1 (.in(logic_1_p1[0]));
  LED led_2 (.in(logic_1_p1[1]));
  LED led_3 (.in(logic_1_p1[2]));
  LED led_4 (.in(logic_1_p1[3]));
  LED led_5 (.in(logic_1_p1[4]));
  LED led_6 (.in(logic_1_p1[5]));
  LED led_7 (.in(logic_1_p1[6]));
  LED led_8 (.in(logic_1_p1[7]));
  // ProgramCounter programcounter_1: pin names not known; wires that end beside it: CK, 1'b1, programcounter_1_p3, programcounter_1_p4, programcounter_1_p5
  RAMDualPort #(.AddrBits(4), .isProgramMemory("true"), .Bits(4)) ramdualport_1 (
    .A(logic_1_p2), .Din(_4x4bit_registers_1__4b_out_2), .str(logic_1_p10), .C(CK), .ld(ram_OE),
    .D(ramdualport_1_d));
  Button button_1 (.out(programcounter_1_p4));
  Add #(.Bits(8)) PC_increment (.a(programcounter_1_p5), .b(8'h1), .c_i(1'b0), .s(programcounter_1_p3));  // open: c_o
  LED led_9 (.in(programcounter_1_p3[0]));
  LED led_10 (.in(programcounter_1_p3[1]));
  LED led_11 (.in(programcounter_1_p3[2]));
  LED led_12 (.in(programcounter_1_p3[3]));
  LED led_13 (.in(programcounter_1_p3[4]));
  LED led_14 (.in(programcounter_1_p3[5]));
  LED led_15 (.in(programcounter_1_p3[6]));
  LED led_16 (.in(programcounter_1_p3[7]));

  // Notes on the sheet:
  //   contents of eeprom_1 (hex, n*v repeats v):
  //   17,37,22,86
endmodule
