// Digital circuit D-latch.dig as structural Verilog
module D_latch (
  input  D,
  input  CK,
  input  R,
  output Q,
  output Q_2
);

  wire and_1_out, and_2_out, not_1_out;

  not not_1 (not_1_out, D);
  and and_1 (and_1_out, D, CK);
  and and_2 (and_2_out, CK, not_1_out);
  nor nor_1 (Q, and_2_out, R, Q_2);
  nor nor_2 (Q_2, and_1_out, Q);
endmodule
