// Digital circuit FlipFlop_D.dig as structural Verilog
module FlipFlop_D (
  input  CK,
  input  D,
  input  Write_enable,
  input  R,
  output Q,
  output Q_2
);

  wire and_1_out, d_latch_1_q, not_1_out;

  and and_1 (and_1_out, Write_enable, CK);
  D_latch d_latch_1 (.D(D), .CK(and_1_out), .R(R), .Q(d_latch_1_q));  // open: Q_2
  not not_1 (not_1_out, and_1_out);
  D_latch d_latch_2 (.D(d_latch_1_q), .CK(not_1_out), .R(R), .Q(Q), .Q_2(Q_2));
endmodule
