// Digital circuit flip-flop.dig as structural Verilog
module flip_flop (
  input  S,
  input  CK,
  input  R,
  output Q,
  output Q_2
);

  wire nand_1_out, nand_2_out;

  nand nand_1 (nand_1_out, S, CK);
  nand nand_2 (nand_2_out, CK, R);
  nand nand_3 (Q, nand_1_out, Q_2);
  nand nand_4 (Q_2, nand_2_out, Q);
endmodule
