// Digital circuit logic.dig as structural Verilog
module \logic  (
  input  [7:0] Dbus,
  input  [7:0] reg_bus,
  output S0,
  output S1,
  output S2,
  output S3,
  output S4,
  output S5,
  output WE1,
  output WE2,
  output RAM_OE,
  output carry_in,
  output WE_PC,
  output S6,
  output S7
);

  wire [7:4] rom_1_d;

  ROM #(.AddrBits(4), .Bits(10)) rom_1 (.A(Dbus[7:4]), .sel(1'b1), .D({S7, S6, rom_1_d, RAM_OE, WE_PC, WE2, WE1}));
  or or_1 (S2, rom_1_d[4], Dbus[2]);
  or or_2 (S3, Dbus[3], rom_1_d[5]);
  or or_3 (S4, rom_1_d[6], Dbus[0]);
  or or_4 (S5, rom_1_d[7], Dbus[1]);

  assign carry_in = Dbus[2];
  assign S0 = Dbus[0];
  assign S1 = Dbus[1];

  // Other names for the same wires on the sheet: s2_t = Dbus[2]; s3_t = Dbus[3]

  // Notes on the sheet:
  //   contents of rom_1 (hex, n*v repeats v):
  //   0,0,371,101,1,201,2,9
endmodule
